// Logisim project rudimentary computing device.circ as structural Verilog: 1 circuit, main circuit main
module main (
  input  in_1,
  input  in_2,
  input  in_3,
  input  in_4,
  input  in_5,
  input  in_6,
  input  in_7
);

  wire clock_1_out, main_1_out_9, main_1_out_10, main_1_out_11, main_1_out_12, main_1_out_13, main_1_out_14;

  Clock clock_1 (.out(clock_1_out));
  LED led_1 (.in(main_1_out_12));
  LED led_2 (.in(main_1_out_9));
  LED led_3 (.in(main_1_out_10));
  LED led_4 (.in(main_1_out_11));
  program_counter_main main_1 (
    .in_7(in_1), .in_8(clock_1_out), .out_9(main_1_out_9), .out_10(main_1_out_10), .out_11(main_1_out_11),
    .out_12(main_1_out_12), .out_13(main_1_out_13), .out_14(main_1_out_14), .in_1(in_2), .in_2(in_3),
    .in_3(in_4), .in_4(in_5), .in_5(in_6), .in_6(in_7));
  LED led_5 (.in(main_1_out_13));
  LED led_6 (.in(main_1_out_14));
endmodule
